# Fritzing sketch cables (saved by Fritzing 0.9.3b)

parts:
  Raspberry_Pi_1 = Raspberry Pi 3 [part_number=RPI-3-V1.2]
  J1 = Basic Servo
  J2 = Basic Servo
  U1 = mystery part, 4 pins [chip_label=Fan]

nets:
  N1: Raspberry_Pi_1.GPIO4, J2.pulse
  GND: Raspberry_Pi_1.GND, J1.gnd, J2.gnd, U1.pin2
  N2: Raspberry_Pi_1.GPIO17, J1.pulse
  N3: Raspberry_Pi_1.3V3, U1.pin1
  VCC: Raspberry_Pi_1.5V, J1.vcc, J2.vcc

notes:
  ESC avec Alim + Moteur
